# Fritzing sketch EC Wiring (saved by Fritzing 0.9.3b)
breadboards: 1

parts:
  Part1 = Arduino Leonardo (Rev3b)
  R1 = Resistor [tolerance=±5% resistance=4.7k package=THT]
  R2 = Resistor [tolerance=±5% resistance=1k package=THT]
  DS1 = DS18B20 1-Wire Temperature Sensor [part_number=DS18B20]
  J1 = Power Jack [package=power_jack_slot]

nets:
  N1: Part1.D2/SDA, R1.Pin_0, DS1.DQ
  5V: Part1.5V, R1.Pin_1, DS1.VDD
  GND: Part1.GND, DS1.GND, J1.GNDBREAK
  N2: Part1.A0, R2.Pin_0, J1.PWR
  N3: Part1.A4, R2.Pin_1
